// Logisim project CPU.circ as structural Verilog: 5 circuits, main circuit MAIN
module MAIN (
  input  in_1,
  input  RST,
  input  PCR,
  input  PCW,
  input  PCI,
  input  MAW,
  input  IRW,
  input  DRR,
  input  DRW,
  input  MMR,
  input  MMW,
  input  ARR,
  input  ARW,
  input  BRR,
  input  BRW,
  input  in_16,
  input  in_17,
  input  in_18,
  input  in_19
);

  wire and_1_out, and_2_out, com_clk_1_clk, or_1_out, STEP_out;
  wire [7:0] INSTRUCTION_REGISTER_data_out, MEMADDR_REGISTER_data_out, PROGRAM_COUNTER_data_out, ram_1_dout,
       rom_1_data, STEP_COUNTER_data_out;

  LED led_1 (.in(PROGRAM_COUNTER_data_out[7]));
  LED led_2 (.in(PROGRAM_COUNTER_data_out[6]));
  LED led_3 (.in(PROGRAM_COUNTER_data_out[5]));
  Button STEP (.out(STEP_out));
  LED led_4 (.in(PROGRAM_COUNTER_data_out[4]));
  LED led_5 (.in(PROGRAM_COUNTER_data_out[3]));
  LED led_6 (.in(PROGRAM_COUNTER_data_out[2]));
  LED led_7 (.in(PROGRAM_COUNTER_data_out[1]));
  LED led_8 (.in(PROGRAM_COUNTER_data_out[0]));
  COM_CLK com_clk_1 (.HALT(in_1), .STEP(STEP_out), .CLK(com_clk_1_clk));
  COM_CNT PROGRAM_COUNTER (
    .READ(PCR), .WRITE(PCW), .INC(PCI), .RESET(RST), .CLK(com_clk_1_clk), .DATA_IN(PROGRAM_COUNTER_data_out),
    .DATA_OUT(PROGRAM_COUNTER_data_out));  // open: CARRY
  COM_REG A_REGISTER (
    .DATA_IN(PROGRAM_COUNTER_data_out), .READ(ARR), .WRITE(ARW), .RESET(in_19), .CLK(com_clk_1_clk),
    .DATA_OUT(PROGRAM_COUNTER_data_out));
  COM_REG B_REGISTER (
    .DATA_IN(PROGRAM_COUNTER_data_out), .READ(BRR), .WRITE(BRW), .RESET(com_clk_1_clk), .CLK(BRR),
    .DATA_OUT(PROGRAM_COUNTER_data_out));
  COM_REG MEMADDR_REGISTER (
    .DATA_IN(PROGRAM_COUNTER_data_out), .READ(MMR), .WRITE(MAW), .RESET(RST), .CLK(com_clk_1_clk),
    .DATA_OUT(MEMADDR_REGISTER_data_out));
  ROM #(.addrWidth(7)) rom_1 (.addr(MEMADDR_REGISTER_data_out[6:0]), .data(rom_1_data));
  RAM #(.addrWidth(7)) ram_1 (
    .addr(MEMADDR_REGISTER_data_out[6:0]), .we(MMW), .oe(MMR), .clk(com_clk_1_clk),
    .din(PROGRAM_COUNTER_data_out), .dout(ram_1_dout));
  assign PROGRAM_COUNTER_data_out = and_2_out ? ram_1_dout : 8'bz;  // Controlled_Buffer controlled_buffer_1
  and and_1 (and_1_out, ~MEMADDR_REGISTER_data_out[7], MMR);  // AND_Gate
  assign PROGRAM_COUNTER_data_out = and_1_out ? rom_1_data : 8'bz;  // Controlled_Buffer controlled_buffer_2
  and and_2 (and_2_out, MEMADDR_REGISTER_data_out[7], MMR);
  or or_1 (or_1_out, RST, STEP_COUNTER_data_out[4]);
  COM_CNT STEP_COUNTER (
    .READ(1'b1), .INC(1'b1), .RESET(or_1_out), .CLK(com_clk_1_clk), .DATA_OUT(STEP_COUNTER_data_out));  // open: WRITE, DATA_IN, CARRY
  COM_REG INSTRUCTION_REGISTER (
    .DATA_IN(PROGRAM_COUNTER_data_out), .READ(1'b1), .WRITE(IRW), .RESET(RST), .CLK(com_clk_1_clk),
    .DATA_OUT(INSTRUCTION_REGISTER_data_out));
  COM_REG DATA_REGISTER (
    .DATA_IN(PROGRAM_COUNTER_data_out), .READ(DRR), .WRITE(DRW), .RESET(RST), .CLK(com_clk_1_clk),
    .DATA_OUT(PROGRAM_COUNTER_data_out));
  ROM #(.addrWidth(12)) rom_2 (
    .addr({INSTRUCTION_REGISTER_data_out, STEP_COUNTER_data_out[3:0]}),
    .data({in_18, in_17, in_16, BRW, BRR, ARW, ARR, MMW}));
  ROM #(.addrWidth(12)) rom_3 (
    .addr({INSTRUCTION_REGISTER_data_out, STEP_COUNTER_data_out[3:0]}),
    .data({MMR, DRW, DRR, IRW, MAW, PCI, PCW, PCR}));

  // Notes on the sheet:
  //   contents of rom_1 (hex, n*v repeats v):
  //   0 4
  //   contents of rom_3 (hex, n*v repeats v):
  //   9 94 9 82 12*0 9 94
  //   MICROCODE_BYTE_HIGH
  //   MICROCODE_BYTE_LOW
endmodule

module COM_ALU (
  input  [7:0] INPUT_A,
  input  [7:0] INPUT_B,
  input  CARRY,
  input  OP_ADD,
  input  OP_SUB,
  input  OP_AND,
  input  OP_OR,
  input  OP_XOR,
  input  OP_NOT,
  output [7:0] RESULT,
  output CARRY_FLAG,
  output OFLOW_FLAG,
  output SIGN_FLAG,
  output ZERO_FLAG
);

  wire and_1_out, and_2_out, and_3_out, and_4_out, and_5_out, and_6_out, and_7_out, and_8_out, and_9_out,
       and_10_out, and_11_out, and_12_out, and_13_out, and_14_out, and_15_out, and_16_out, and_18_out,
       and_20_out, and_21_out, and_22_out, nor_1_out, nor_2_out, nor_3_out, or_1_out, or_2_out, or_3_out,
       or_4_out, or_5_out, or_6_out, or_7_out, or_8_out, or_9_out, or_11_out, or_12_out, or_13_out,
       or_14_out, or_15_out, or_16_out, xor_2_out, xor_3_out, xor_4_out, xor_5_out, xor_6_out, xor_7_out,
       xor_8_out, xor_9_out;
  wire [7:0] and_17_out, not_1_out, or_10_out, xor_1_out, xor_10_out, xor_18_out;

  assign xor_1_out = INPUT_B ^ {8{OP_SUB}};  // XOR_Gate xor_1, 8 bits wide
  or or_1 (or_1_out, CARRY, OP_SUB);
  xor xor_2 (xor_2_out, INPUT_A[0], xor_1_out[0]);
  and and_1 (and_1_out, INPUT_A[0], xor_1_out[0]);
  xor xor_3 (xor_3_out, INPUT_A[1], xor_1_out[1]);
  and and_2 (and_2_out, INPUT_A[1], xor_1_out[1]);
  xor xor_4 (xor_4_out, INPUT_A[2], xor_1_out[2]);
  and and_3 (and_3_out, INPUT_A[2], xor_1_out[2]);
  xor xor_5 (xor_5_out, INPUT_A[3], xor_1_out[3]);
  and and_4 (and_4_out, INPUT_A[3], xor_1_out[3]);
  xor xor_6 (xor_6_out, INPUT_A[4], xor_1_out[4]);
  and and_5 (and_5_out, INPUT_A[4], xor_1_out[4]);
  xor xor_7 (xor_7_out, INPUT_A[5], xor_1_out[5]);
  and and_6 (and_6_out, INPUT_A[5], xor_1_out[5]);
  xor xor_8 (xor_8_out, INPUT_A[6], xor_1_out[6]);
  and and_7 (and_7_out, INPUT_A[6], xor_1_out[6]);
  xor xor_9 (xor_9_out, INPUT_A[7], xor_1_out[7]);
  and and_8 (and_8_out, INPUT_A[7], xor_1_out[7]);
  xor xor_10 (xor_10_out[0], xor_2_out, or_1_out);
  and and_9 (and_9_out, xor_2_out, or_1_out);
  or or_2 (or_2_out, and_9_out, and_1_out);
  xor xor_11 (xor_10_out[1], xor_3_out, or_2_out);
  and and_10 (and_10_out, xor_3_out, or_2_out);
  or or_3 (or_3_out, and_10_out, and_2_out);
  xor xor_12 (xor_10_out[2], xor_4_out, or_3_out);
  and and_11 (and_11_out, xor_4_out, or_3_out);
  or or_4 (or_4_out, and_11_out, and_3_out);
  xor xor_13 (xor_10_out[3], xor_5_out, or_4_out);
  and and_12 (and_12_out, xor_5_out, or_4_out);
  or or_5 (or_5_out, and_12_out, and_4_out);
  xor xor_14 (xor_10_out[4], xor_6_out, or_5_out);
  and and_13 (and_13_out, xor_6_out, or_5_out);
  or or_6 (or_6_out, and_13_out, and_5_out);
  xor xor_15 (xor_10_out[5], xor_7_out, or_6_out);
  and and_14 (and_14_out, xor_7_out, or_6_out);
  or or_7 (or_7_out, and_14_out, and_6_out);
  xor xor_16 (xor_10_out[6], xor_8_out, or_7_out);
  and and_15 (and_15_out, xor_8_out, or_7_out);
  or or_8 (or_8_out, and_15_out, and_7_out);
  xor xor_17 (xor_10_out[7], xor_9_out, or_8_out);
  and and_16 (and_16_out, xor_9_out, or_8_out);
  or or_9 (or_9_out, and_16_out, and_8_out);
  assign and_17_out = INPUT_A & xor_1_out;  // AND_Gate and_17, 8 bits wide
  assign or_10_out = INPUT_A | xor_1_out;  // OR_Gate or_10, 8 bits wide
  assign xor_18_out = INPUT_A ^ xor_1_out;  // XOR_Gate xor_18, 8 bits wide
  assign not_1_out = ~INPUT_A;  // NOT_Gate not_1, 8 bits wide
  assign RESULT = or_11_out ? xor_10_out : 8'bz;  // Controlled_Buffer controlled_buffer_1
  or or_11 (or_11_out, OP_ADD, OP_SUB);
  and and_18 (and_18_out, or_11_out, or_9_out);
  and and_19 (OFLOW_FLAG, or_11_out, or_12_out);
  nor nor_1 (nor_1_out, INPUT_A[7], xor_1_out[7]);
  and and_20 (and_20_out, INPUT_A[7], xor_1_out[7]);
  xor xor_19 (CARRY_FLAG, OP_SUB, and_18_out);
  or or_12 (or_12_out, and_21_out, and_22_out);
  and and_21 (and_21_out, nor_1_out, xor_10_out[7]);
  and and_22 (and_22_out, and_20_out, ~xor_10_out[7]);  // AND_Gate
  assign RESULT = OP_AND ? and_17_out : 8'bz;  // Controlled_Buffer controlled_buffer_2
  assign RESULT = OP_OR ? or_10_out : 8'bz;  // Controlled_Buffer controlled_buffer_3
  assign RESULT = OP_XOR ? xor_18_out : 8'bz;  // Controlled_Buffer controlled_buffer_4
  assign RESULT = OP_NOT ? not_1_out : 8'bz;  // Controlled_Buffer controlled_buffer_5
  or or_13 (or_13_out, RESULT[7], RESULT[6]);
  nor nor_2 (nor_2_out, or_13_out, or_14_out);
  or or_14 (or_14_out, RESULT[5], RESULT[4]);
  or or_15 (or_15_out, RESULT[3], RESULT[2]);
  nor nor_3 (nor_3_out, or_15_out, or_16_out);
  and and_23 (ZERO_FLAG, nor_2_out, nor_3_out);
  or or_16 (or_16_out, RESULT[1], RESULT[0]);

  assign SIGN_FLAG = RESULT[7];
endmodule

module COM_CLK (
  input  HALT,
  input  STEP,
  output CLK
);

  wire and_1_out, clock_1_out, not_1_out, or_1_out;

  Clock clock_1 (.out(clock_1_out));
  not not_1 (not_1_out, HALT);
  or or_1 (or_1_out, not_1_out, STEP);
  and and_1 (and_1_out, clock_1_out, or_1_out);
  or or_2 (CLK, and_1_out, STEP);
endmodule

module COM_REG (
  input  [7:0] DATA_IN,
  input  READ,
  input  WRITE,
  input  RESET,
  input  CLK,
  output [7:0] DATA_OUT
);

  wire and_1_out, and_2_out, and_3_out, and_4_out, and_5_out, and_6_out, and_7_out, and_8_out, and_9_out,
       and_10_out, and_11_out, and_12_out, and_13_out, and_14_out, and_15_out, and_16_out, d_ff_1_q,
       d_ff_2_q, d_ff_3_q, d_ff_4_q, d_ff_5_q, d_ff_6_q, d_ff_7_q, d_ff_8_q, or_1_out, or_2_out, or_3_out,
       or_4_out, or_5_out, or_6_out, or_7_out, or_8_out;

  and and_1 (and_1_out, WRITE, DATA_IN[0]);
  and and_2 (and_2_out, ~WRITE, d_ff_1_q);  // AND_Gate
  or or_1 (or_1_out, and_1_out, and_2_out);
  D_Flip_Flop #(.trigger("falling")) d_ff_1 (.D(or_1_out), .clk(CLK), .Q(d_ff_1_q), .reset(RESET));  // open: Qn, preset
  assign DATA_OUT[0] = READ ? d_ff_1_q : 1'bz;  // Controlled_Buffer controlled_buffer_1
  and and_3 (and_3_out, WRITE, DATA_IN[1]);
  or or_2 (or_2_out, and_3_out, and_4_out);
  D_Flip_Flop #(.trigger("falling")) d_ff_2 (.D(or_2_out), .clk(CLK), .Q(d_ff_2_q), .reset(RESET));  // open: Qn, preset
  assign DATA_OUT[1] = READ ? d_ff_2_q : 1'bz;  // Controlled_Buffer controlled_buffer_2
  and and_4 (and_4_out, ~WRITE, d_ff_2_q);  // AND_Gate
  and and_5 (and_5_out, WRITE, DATA_IN[2]);
  assign DATA_OUT[2] = READ ? d_ff_3_q : 1'bz;  // Controlled_Buffer controlled_buffer_3
  and and_6 (and_6_out, ~WRITE, d_ff_3_q);  // AND_Gate
  or or_3 (or_3_out, and_5_out, and_6_out);
  D_Flip_Flop #(.trigger("falling")) d_ff_3 (.D(or_3_out), .clk(CLK), .Q(d_ff_3_q), .reset(RESET));  // open: Qn, preset
  and and_7 (and_7_out, WRITE, DATA_IN[3]);
  and and_8 (and_8_out, ~WRITE, d_ff_4_q);  // AND_Gate
  or or_4 (or_4_out, and_7_out, and_8_out);
  D_Flip_Flop #(.trigger("falling")) d_ff_4 (.D(or_4_out), .clk(CLK), .Q(d_ff_4_q), .reset(RESET));  // open: Qn, preset
  assign DATA_OUT[3] = READ ? d_ff_4_q : 1'bz;  // Controlled_Buffer controlled_buffer_4
  and and_9 (and_9_out, WRITE, DATA_IN[4]);
  and and_10 (and_10_out, ~WRITE, d_ff_5_q);  // AND_Gate
  or or_5 (or_5_out, and_9_out, and_10_out);
  D_Flip_Flop #(.trigger("falling")) d_ff_5 (.D(or_5_out), .clk(CLK), .Q(d_ff_5_q), .reset(RESET));  // open: Qn, preset
  assign DATA_OUT[4] = READ ? d_ff_5_q : 1'bz;  // Controlled_Buffer controlled_buffer_5
  and and_11 (and_11_out, WRITE, DATA_IN[5]);
  or or_6 (or_6_out, and_11_out, and_12_out);
  D_Flip_Flop #(.trigger("falling")) d_ff_6 (.D(or_6_out), .clk(CLK), .Q(d_ff_6_q), .reset(RESET));  // open: Qn, preset
  assign DATA_OUT[5] = READ ? d_ff_6_q : 1'bz;  // Controlled_Buffer controlled_buffer_6
  and and_12 (and_12_out, ~WRITE, d_ff_6_q);  // AND_Gate
  and and_13 (and_13_out, WRITE, DATA_IN[6]);
  assign DATA_OUT[6] = READ ? d_ff_7_q : 1'bz;  // Controlled_Buffer controlled_buffer_7
  and and_14 (and_14_out, ~WRITE, d_ff_7_q);  // AND_Gate
  or or_7 (or_7_out, and_13_out, and_14_out);
  D_Flip_Flop #(.trigger("falling")) d_ff_7 (.D(or_7_out), .clk(CLK), .Q(d_ff_7_q), .reset(RESET));  // open: Qn, preset
  and and_15 (and_15_out, WRITE, DATA_IN[7]);
  and and_16 (and_16_out, ~WRITE, d_ff_8_q);  // AND_Gate
  or or_8 (or_8_out, and_15_out, and_16_out);
  D_Flip_Flop #(.trigger("falling")) d_ff_8 (.D(or_8_out), .clk(CLK), .Q(d_ff_8_q), .reset(RESET));  // open: Qn, preset
  assign DATA_OUT[7] = READ ? d_ff_8_q : 1'bz;  // Controlled_Buffer controlled_buffer_8
endmodule

module COM_CNT (
  input  [7:0] DATA_IN,
  input  READ,
  input  WRITE,
  input  INC,
  input  RESET,
  input  CLK,
  output [7:0] DATA_OUT,
  output CARRY
);

  wire and_1_out, and_2_out, and_3_out, and_4_out, and_5_out, and_6_out, and_7_out, and_8_out, and_9_out,
       and_10_out, and_11_out, and_12_out, and_13_out, and_14_out, and_15_out, and_16_out, and_17_out,
       and_18_out, and_19_out, and_20_out, and_21_out, and_22_out, and_23_out, and_24_out, and_25_out,
       and_26_out, and_27_out, and_28_out, and_29_out, and_30_out, j_k_ff_1_q, j_k_ff_2_q, j_k_ff_3_q,
       j_k_ff_4_q, j_k_ff_5_q, j_k_ff_6_q, j_k_ff_7_q, j_k_ff_8_q, or_1_out, or_2_out, or_3_out, or_4_out,
       or_5_out, or_6_out, or_7_out, or_8_out, or_9_out, or_10_out, or_11_out, or_12_out, or_13_out,
       or_14_out, or_15_out, or_16_out;

  and and_1 (and_1_out, ~DATA_IN[0], WRITE);  // AND_Gate
  or or_1 (or_1_out, INC, and_1_out);
  or or_2 (or_2_out, INC, and_2_out);
  assign DATA_OUT[0] = READ ? j_k_ff_1_q : 1'bz;  // Controlled_Buffer controlled_buffer_1
  and and_2 (and_2_out, DATA_IN[0], WRITE);
  J_K_Flip_Flop #(.trigger("falling")) j_k_ff_1 (
    .J(or_2_out), .K(or_1_out), .clk(CLK), .Q(j_k_ff_1_q), .reset(RESET));  // open: Qn, preset
  and and_3 (and_3_out, ~DATA_IN[1], WRITE);  // AND_Gate
  and and_4 (and_4_out, INC, j_k_ff_1_q);
  or or_3 (or_3_out, and_4_out, and_3_out);
  and and_5 (and_5_out, DATA_IN[1], WRITE);
  or or_4 (or_4_out, and_4_out, and_5_out);
  J_K_Flip_Flop #(.trigger("falling")) j_k_ff_2 (
    .J(or_4_out), .K(or_3_out), .clk(CLK), .Q(j_k_ff_2_q), .reset(RESET));  // open: Qn, preset
  assign DATA_OUT[1] = READ ? j_k_ff_2_q : 1'bz;  // Controlled_Buffer controlled_buffer_2
  and and_6 (and_6_out, INC, and_7_out);
  and and_7 (and_7_out, j_k_ff_2_q, j_k_ff_1_q);
  and and_8 (and_8_out, ~DATA_IN[2], WRITE);  // AND_Gate
  and and_9 (and_9_out, DATA_IN[2], WRITE);
  or or_5 (or_5_out, and_6_out, and_8_out);
  or or_6 (or_6_out, and_6_out, and_9_out);
  J_K_Flip_Flop #(.trigger("falling")) j_k_ff_3 (
    .J(or_6_out), .K(or_5_out), .clk(CLK), .Q(j_k_ff_3_q), .reset(RESET));  // open: Qn, preset
  assign DATA_OUT[2] = READ ? j_k_ff_3_q : 1'bz;  // Controlled_Buffer controlled_buffer_3
  and and_10 (and_10_out, j_k_ff_3_q, and_7_out);
  and and_11 (and_11_out, ~DATA_IN[3], WRITE);  // AND_Gate
  and and_12 (and_12_out, INC, and_10_out);
  or or_7 (or_7_out, and_12_out, and_11_out);
  assign DATA_OUT[3] = READ ? j_k_ff_4_q : 1'bz;  // Controlled_Buffer controlled_buffer_4
  and and_13 (and_13_out, DATA_IN[3], WRITE);
  or or_8 (or_8_out, and_12_out, and_13_out);
  J_K_Flip_Flop #(.trigger("falling")) j_k_ff_4 (
    .J(or_8_out), .K(or_7_out), .clk(CLK), .Q(j_k_ff_4_q), .reset(RESET));  // open: Qn, preset
  and and_14 (and_14_out, INC, and_15_out);
  and and_15 (and_15_out, j_k_ff_4_q, and_10_out);
  or or_9 (or_9_out, and_14_out, and_17_out);
  and and_16 (and_16_out, DATA_IN[4], WRITE);
  and and_17 (and_17_out, ~DATA_IN[4], WRITE);  // AND_Gate
  or or_10 (or_10_out, and_14_out, and_16_out);
  J_K_Flip_Flop #(.trigger("falling")) j_k_ff_5 (
    .J(or_10_out), .K(or_9_out), .clk(CLK), .Q(j_k_ff_5_q), .reset(RESET));  // open: Qn, preset
  assign DATA_OUT[4] = READ ? j_k_ff_5_q : 1'bz;  // Controlled_Buffer controlled_buffer_5
  and and_18 (and_18_out, j_k_ff_5_q, and_15_out);
  and and_19 (and_19_out, ~DATA_IN[5], WRITE);  // AND_Gate
  and and_20 (and_20_out, DATA_IN[5], WRITE);
  and and_21 (and_21_out, INC, and_18_out);
  or or_11 (or_11_out, and_21_out, and_19_out);
  or or_12 (or_12_out, and_21_out, and_20_out);
  assign DATA_OUT[5] = READ ? j_k_ff_6_q : 1'bz;  // Controlled_Buffer controlled_buffer_6
  and and_22 (and_22_out, j_k_ff_6_q, and_18_out);
  J_K_Flip_Flop #(.trigger("falling")) j_k_ff_6 (
    .J(or_12_out), .K(or_11_out), .clk(CLK), .Q(j_k_ff_6_q), .reset(RESET));  // open: Qn, preset
  and and_23 (and_23_out, ~DATA_IN[6], WRITE);  // AND_Gate
  and and_24 (and_24_out, INC, and_22_out);
  or or_13 (or_13_out, and_24_out, and_23_out);
  and and_25 (and_25_out, DATA_IN[6], WRITE);
  or or_14 (or_14_out, and_24_out, and_25_out);
  J_K_Flip_Flop #(.trigger("falling")) j_k_ff_7 (
    .J(or_14_out), .K(or_13_out), .clk(CLK), .Q(j_k_ff_7_q), .reset(RESET));  // open: Qn, preset
  assign DATA_OUT[6] = READ ? j_k_ff_7_q : 1'bz;  // Controlled_Buffer controlled_buffer_7
  and and_26 (and_26_out, INC, and_27_out);
  and and_27 (and_27_out, j_k_ff_7_q, and_22_out);
  and and_28 (and_28_out, ~DATA_IN[7], WRITE);  // AND_Gate
  and and_29 (and_29_out, DATA_IN[7], WRITE);
  or or_15 (or_15_out, and_26_out, and_28_out);
  or or_16 (or_16_out, and_26_out, and_29_out);
  J_K_Flip_Flop #(.trigger("falling")) j_k_ff_8 (
    .J(or_16_out), .K(or_15_out), .clk(CLK), .Q(j_k_ff_8_q), .reset(RESET));  // open: Qn, preset
  assign DATA_OUT[7] = READ ? j_k_ff_8_q : 1'bz;  // Controlled_Buffer controlled_buffer_8
  and and_30 (and_30_out, j_k_ff_8_q, and_27_out);
  and and_31 (CARRY, INC, and_30_out);
endmodule
